# Fritzing sketch Door Status Sign - DOOR SIGN Fritzing Diagram (saved by Fritzing 0.9.9b)
breadboards: 1

parts:
  J1 = nRF24L01+
  LED1 = LED - 5mm [color="Red (633nm)" current=0.030 package="5 mm [THT]"]
  LED2 = LED - 5mm [color="Blue (525nm)" current=0.030 package="5 mm [THT]"]
  LED3 = LED - 5mm [color="Yellow (595nm)" current=0.030 package="5 mm [THT]"]
  LED4 = LED - 5mm [color="Green (565nm)" current=0.030 package="5 mm [THT]"]
  LED5 = RGB LED (com. cathode, rgb) [package="5 mm [THT]"]
  LCD1 = LCD screen
  R1 = Resistor [tolerance=±5% power=0.25 resistance=220 package=THT]
  R2 = Resistor [tolerance=±5% power=0.25 resistance=220 package=THT]
  R3 = Resistor [tolerance=±5% power=0.25 resistance=220 package=THT]
  R4 = Resistor [tolerance=±5% power=0.25 resistance=220 package=THT]
  R5 = Resistor [tolerance=±5% power=0.25 resistance=220 package=THT]
  R6 = Resistor [tolerance=±5% power=0.25 resistance=220 package=THT]
  R7 = Resistor [tolerance=±5% power=0.25 resistance=220 package=THT]
  Part1 = Arduino Mega 2560 (Rev3)
  LCM1602_IIC1 = LCM1602 IIC [part_number="LCM1602 IIC" chip_label="LCM1602 IIC" package="DIP (Dual Inline) [THT]"]
  S2 = Pushbutton [package="[THT]"]

nets:
  VCC: J1.VCC, Part1.5V, LCM1602_IIC1.VCC
  GND: J1.GND, LED1.cathode, LED2.cathode, LED3.cathode, LED4.cathode, LED5.common_cathode, Part1.GND, LCM1602_IIC1.GND, S2.Pin_3, S2.Pin_4
  N1: J1.CSN, Part1.D8_PWM
  N2: J1.CE, Part1.D9_PWM
  N3: J1.MOSI, Part1.D51
  N4: J1.SCK, Part1.D52
  N5: J1.MISO, Part1.D50
  N6: LED1.anode, R1.Pin_0
  N7: LED2.anode, R4.Pin_0, Part1.D25
  N8: LED3.anode, R2.Pin_0
  N9: LED4.anode, R3.Pin_0, Part1.D24
  N10: LED5.red_anode, R5.Pin_0
  N11: LED5.green_anode, R6.Pin_0
  N12: LED5.blue_anode, R7.Pin_0
  VSS: LCD1.VSS, LCM1602_IIC1.VSS
  VDD: LCD1.VDD, LCM1602_IIC1.VDD
  N13: LCD1.V0, LCM1602_IIC1.V0
  N14: LCD1.RS, LCM1602_IIC1.RS
  N15: LCD1.R/W, LCM1602_IIC1.RW
  N16: LCD1.E, LCM1602_IIC1.E
  N17: LCD1.DB0, LCM1602_IIC1.D0
  N18: LCD1.DB1, LCM1602_IIC1.D1
  N19: LCD1.DB2, LCM1602_IIC1.D2
  N20: LCD1.DB3, LCM1602_IIC1.D3
  N21: LCD1.DB4, LCM1602_IIC1.D4
  N22: LCD1.DB5, LCM1602_IIC1.D5
  N23: LCD1.DB6, LCM1602_IIC1.D6
  N24: LCD1.DB7, LCM1602_IIC1.D7
  N25: LCD1.LED+, LCM1602_IIC1.A
  N26: LCD1.LED-, LCM1602_IIC1.K
  N27: R1.Pin_1, Part1.D22
  N28: R2.Pin_1, Part1.D23
  N29: R5.Pin_1, Part1.D30
  N30: R6.Pin_1, Part1.D33
  N31: R7.Pin_1, Part1.D32
  N32: Part1.D21/SCL, LCM1602_IIC1.SCL
  N33: Part1.D20/SDA, LCM1602_IIC1.SDA
  N34: Part1.D36, S2.Pin_1, S2.Pin_2
  N35: LCM1602_IIC1.LED_A, LCM1602_IIC1.LED_B

custom parts:
  nRF24L01+: nRF24L01+ Transceiver
  LCM1602 IIC: I2C-Module to use a 1602 or 2004 LCD on with the wire.h libory Serial LCD Modul
