# Fritzing sketch Door Status Sign - REMOTE Fritzing Diagram (saved by Fritzing 0.9.9b)
breadboards: 1

parts:
  J1 = nRF24L01+
  LED5 = RGB LED (com. cathode, rgb) [package="5 mm [THT]"]
  LCD1 = LCD screen
  R5 = Resistor [tolerance=±5% power=0.25 resistance=220 package=THT]
  R6 = Resistor [tolerance=±5% power=0.25 resistance=220 package=THT]
  R7 = Resistor [tolerance=±5% power=0.25 resistance=220 package=THT]
  Part1 = Arduino Mega 2560 (Rev3)
  LCM1602_IIC1 = LCM1602 IIC [part_number="LCM1602 IIC" chip_label="LCM1602 IIC" package="DIP (Dual Inline) [THT]"]
  S2 = Pushbutton [package="[THT]"]
  S3 = Pushbutton [package="[THT]"]
  S4 = Pushbutton [package="[THT]"]
  S5 = Pushbutton [package="[THT]"]
  J2 = Piezo Speaker
  LED6 = LED - 5mm [color="Red (633nm)" current=0.030 package="5 mm [THT]"]
  R8 = Resistor [tolerance=±5% power=0.25 resistance=220 package=THT]
  S6 = Toggle Switch [package=THT]

nets:
  VCC: J1.VCC, Part1.5V, LCM1602_IIC1.VCC
  GND: J1.GND, LED5.common_cathode, Part1.GND, LCM1602_IIC1.GND, S2.Pin_3, S2.Pin_4, S3.Pin_3, S3.Pin_4, S4.Pin_3, S4.Pin_4, S5.Pin_3, S5.Pin_4, J2.pin1, LED6.cathode, S6.L2
  N1: J1.CSN, Part1.D8_PWM
  N2: J1.CE, Part1.D9_PWM
  N3: J1.MOSI, Part1.D51
  N4: J1.SCK, Part1.D52
  N5: J1.MISO, Part1.D50
  N6: LED5.red_anode, R5.Pin_0
  N7: LED5.green_anode, R6.Pin_0
  N8: LED5.blue_anode, R7.Pin_0
  VSS: LCD1.VSS, LCM1602_IIC1.VSS
  VDD: LCD1.VDD, LCM1602_IIC1.VDD
  N9: LCD1.V0, LCM1602_IIC1.V0
  N10: LCD1.RS, LCM1602_IIC1.RS
  N11: LCD1.R/W, LCM1602_IIC1.RW
  N12: LCD1.E, LCM1602_IIC1.E
  N13: LCD1.DB0, LCM1602_IIC1.D0
  N14: LCD1.DB1, LCM1602_IIC1.D1
  N15: LCD1.DB2, LCM1602_IIC1.D2
  N16: LCD1.DB3, LCM1602_IIC1.D3
  N17: LCD1.DB4, LCM1602_IIC1.D4
  N18: LCD1.DB5, LCM1602_IIC1.D5
  N19: LCD1.DB6, LCM1602_IIC1.D6
  N20: LCD1.DB7, LCM1602_IIC1.D7
  N21: LCD1.LED+, LCM1602_IIC1.A
  N22: LCD1.LED-, LCM1602_IIC1.K
  N23: R5.Pin_1, Part1.D30
  N24: R6.Pin_1, Part1.D31
  N25: R7.Pin_1, Part1.D32
  N26: Part1.D21/SCL, LCM1602_IIC1.SCL
  N27: Part1.D20/SDA, LCM1602_IIC1.SDA
  N28: Part1.D22, S5.Pin_1, S5.Pin_2
  N29: Part1.D23, S4.Pin_1, S4.Pin_2
  N30: Part1.D24, S3.Pin_1, S3.Pin_2
  N31: Part1.D25, S2.Pin_1, S2.Pin_2
  N32: Part1.D36, J2.pin2
  N33: Part1.D40, R8.Pin_1
  N34: Part1.D44, S6.COM
  N35: LCM1602_IIC1.LED_A, LCM1602_IIC1.LED_B
  N36: LED6.anode, R8.Pin_0

custom parts:
  nRF24L01+: nRF24L01+ Transceiver
  LCM1602 IIC: I2C-Module to use a 1602 or 2004 LCD on with the wire.h libory Serial LCD Modul
