# Fritzing sketch Homework 07 Circuit (saved by Fritzing 0.9.9b)
breadboards: 1

parts:
  Part1 = Arduino Uno (Rev3)
  LCM1602_IIC1 = LCM1602 IIC [part_number="LCM1602 IIC" chip_label="LCM1602 IIC" package="DIP (Dual Inline) [THT]"]
  HC-SR04_Sensor_1 = HC-SR04 Ultrasonic Distance Sensor
  J1 = Piezo Speaker
  LED2 = LED - 5mm [color="Red (633nm)" current=0.030 package="5 mm [THT]"]
  R1 = Resistor [tolerance=±5% power=0.25 resistance=220 package=THT]
  S1 = Pushbutton [package="[THT]"]

nets:
  N1: Part1.D9_PWM, LED2.anode
  GND: Part1.GND, LCM1602_IIC1.GND, HC-SR04_Sensor_1.GND, J1.pin1, R1.Pin_1, S1.Pin_3, S1.Pin_4
  N2: Part1.A4/SDA, LCM1602_IIC1.SDA
  N3: Part1.A5/SCL, LCM1602_IIC1.SCL
  N4: Part1.D4, J1.pin2
  N5: Part1.D5_PWM, HC-SR04_Sensor_1.ECHO
  N6: Part1.D6_PWM, HC-SR04_Sensor_1.TRIG
  N7: Part1.D7, S1.Pin_1, S1.Pin_2
  VCC: Part1.5V, LCM1602_IIC1.VCC, HC-SR04_Sensor_1.VCC
  N8: LED2.cathode, R1.Pin_0

custom parts:
  LCM1602 IIC: I2C-Module to use a 1602 or 2004 LCD on with the wire.h libory Serial LCD Modul
