# Fritzing sketch Screen Menus (saved by Fritzing 0.9.9b)
breadboards: 1

parts:
  LCM1602_IIC1 = LCM1602 IIC [part_number="LCM1602 IIC" chip_label="LCM1602 IIC" package="DIP (Dual Inline) [THT]"]
  Part1 = Arduino Mega 2560 (Rev3)
  S1 = Pushbutton [package="[SMD]"]
  S2 = Pushbutton [package="[SMD]"]
  S3 = Pushbutton [package="[SMD]"]
  LED1 = RGB LED (com. cathode, rbg) [package="5 mm [THT]"]
  R1 = Resistor [tolerance=±5% power=0.25 resistance=220 package=THT]
  R2 = Resistor [tolerance=±5% power=0.25 resistance=220 package=THT]
  R3 = Resistor [tolerance=±5% power=0.25 resistance=220 package=THT]

nets:
  GND: LCM1602_IIC1.GND, Part1.GND, S1.Pin_3, S1.Pin_4, S2.Pin_3, S2.Pin_4, S3.Pin_3, S3.Pin_4, LED1.common_cathode
  VCC: LCM1602_IIC1.VCC, Part1.5V
  N1: LCM1602_IIC1.SDA, Part1.D20/SDA
  N2: LCM1602_IIC1.SCL, Part1.D21/SCL
  N3: Part1.D10_PWM, S1.Pin_1, S1.Pin_2
  N4: Part1.D8_PWM, S2.Pin_1, S2.Pin_2
  N5: Part1.D2_PWM, R3.Pin_0
  N6: Part1.D3_PWM, R2.Pin_0
  N7: Part1.D4_PWM, R1.Pin_0
  N8: Part1.D7_PWM, S3.Pin_1, S3.Pin_2
  N9: LED1.red_anode, R1.Pin_1
  N10: LED1.blue_anode, R2.Pin_1
  N11: LED1.green_anode, R3.Pin_1

notes:
  The code for this project is meant to accomodate a 20x4 LCD I2C display; edit code if display differs from accomodations.

custom parts:
  LCM1602 IIC: I2C-Module to use a 1602 or 2004 LCD on with the wire.h libory Serial LCD Modul
