# Fritzing sketch For STEM - Fritzing Diagram (saved by Fritzing 0.9.9b)
breadboards: 1

parts:
  Part1 = Arduino Nano (Rev3.0)
  S1 = Pushbutton [package="[THT]"]
  LED1 = LED - 5mm [color="Green (555nm)" current=0.030 package="5 mm [THT]"]
  LED2 = LED - 5mm [color="Green (555nm)" current=0.030 package="5 mm [THT]"]
  LED3 = LED - 5mm [color="Green (555nm)" current=0.030 package="5 mm [THT]"]
  LED4 = LED - 5mm [color="Red (635nm)" current=0.030 package="5 mm [THT]"]
  R1 = Resistor [tolerance=±5% power=0.25 resistance=220 package=THT]
  R2 = Resistor [tolerance=±5% power=0.25 resistance=220 package=THT]
  R3 = Resistor [tolerance=±5% power=0.25 resistance=220 package=THT]
  R4 = Resistor [tolerance=±5% power=0.25 resistance=220 package=THT]
  M1 = fc-51 [package=THT]
  VCC2 = 4 x AAA Battery Mount

nets:
  N1: Part1.GND, S1.Pin_1, S1.Pin_2, R1.Pin_1, R2.Pin_1, R3.Pin_1, R4.Pin_1, M1.pin3, VCC2.-
  N2: Part1.D2, S1.Pin_3, S1.Pin_4
  N3: Part1.D5, LED4.anode
  N4: Part1.D6, LED3.anode
  N5: Part1.D7, LED2.anode
  N6: Part1.D8, LED1.anode
  N7: Part1.D9, M1.pin1
  N8: Part1.5V, M1.pin2, VCC2.+
  N9: LED1.cathode, R1.Pin_0
  N10: LED2.cathode, R2.Pin_0
  N11: LED3.cathode, R3.Pin_0
  N12: LED4.cathode, R4.Pin_0

// code stored in the sketch: Parts List.ino
/*
Parts Needed:
1 Infrared Sensor
3 Red LEDs
1 Green LED
1 Momentary Pushbutton
4 AAA Batteries
4 220 Ohm Resistors
1 Arduino Nano or equivalent
1 Breadboard
*/

// code stored in the sketch: STEM_Updated_Small_Object_Motion_Detection.ino
int redLed1 = 6;
int redLed2 = 7;
int redLed3 = 8;
int greenLed1 = 5;
int button = 2;
int sensor = 9;

int mode = 1;
int count;
int blinkDelay;
bool sensorMode;

void setup() {
  Serial.begin(9600);

  pinMode(redLed1, OUTPUT);
  pinMode(redLed2, OUTPUT);
  pinMode(redLed3, OUTPUT);
  pinMode(greenLed3, OUTPUT);

  pinMode(button, INPUT_PULLUP);
  pinMode(sensor, INPUT);

  Serial.println("");
  Serial.println("---System Initiated---");
}

void loop() {
  if (mode == 1) { //Awaiting System Setting Mode*************************
    digitalWrite(greenLed1, HIGH);
    Serial.println("Press button to set system mode");

    while (digitalRead(button) == HIGH) {
      // Do nothing while awaiting a button press
    }

    if (digitalRead(sensor) == HIGH) { //Mode: The alarm will be set off if an object is inserted into the view of the sensor
      sensorMode = false;
      Serial.println("Alarm Mode: The alarm will be set off if an object is INSERTED into the view of the sensor");
    }

    if (digitalRead(sensor) == LOW) { //Mode: The alarm will be set off if an object is removed from the view of the sensor
      sensorMode = true;
      Serial.println("Mode: The alarm will be set off if an object is REMOVED from the view of the sensor");
    }

    while (digitalRead(button) == LOW) {
      //Do nothing until the buttun is released
    }

    Serial.println("Press button to initiate countdown");

    while (digitalRead(button) == HIGH) {
      //Do nothing while awaiting a button press
    }

    digitalWrite(greenLed1, LOW);

    mode = 2;
  }

  if (mode == 2) { //Countdown to Ready Mode*************************
    digitalWrite(greenLed2, HIGH);
    Serial.println("Countdown initiated");


    digitalWrite(redLed, HIGH);
    delay(5000);
    digitalWrite(redLed, LOW);

    digitalWrite(greenLed2, LOW);
    Serial.println("Countdown concluded");

    mode = 3;
  }

  if (mode == 3) { //Active Mode*************************
    digitalWrite(greenLed3, HIGH);
    blinkDelay = 1000;

    delay(100);

    Serial.println("Sentinel mode initiated");

    while ((sensorMode == false) && (mode == 3)) {
      if (digitalRead(sensor) == LOW) {
        digitalWrite(greenLed3, LOW);
        mode = 4;
      }
    }

    while ((sensorMode == true) && (mode == 3)) {
      if (digitalRead(sensor) == HIGH) {
        digitalWrite(greenLed3, LOW);
        mode = 4;
      }
    }

  }

  if (mode == 4) { //Alarm Activated Mode*************************
    Serial.println("Sentinal mode disengaged");
    Serial.println("Alarm triggered");

    while (mode == 4) {
      digitalWrite(redLed, HIGH);
      delay(1000);
      digitalWrite(redLed, LOW);
      delay(1000);
    }
  }
}

void countdown() {
  if (count != 0) {
    digitalWrite(redLed, HIGH);
    delay(blinkDelay);
    digitalWrite(redLed, LOW);
    delay(blinkDelay);
    count = count - 1;
  }
}
