# Fritzing sketch Fritzing Diagram - Small Object Motion Dector Guard (saved by Fritzing 0.9.9b)
breadboards: 1

parts:
  Part1 = Arduino Uno (Rev3)
  S1 = Pushbutton [package="[THT]"]
  R1 = Resistor [tolerance=±5% power=0.25 resistance=220 package=THT]
  R2 = Resistor [tolerance=±5% power=0.25 resistance=220 package=THT]
  LED1 = LED - 5mm [color="Red (633nm)" current=0.030 package="5 mm [THT]"]
  LED2 = LED - 5mm [color="Green (560nm)" current=0.030 package="5 mm [THT]"]
  M1 = fc-51 [package=THT]

nets:
  N1: Part1.D12/MISO, R1.Pin_1
  N2: Part1.D13/SCK, R2.Pin_1
  N3: Part1.GND, S1.Pin_1, S1.Pin_2, LED1.cathode, LED2.cathode, M1.pin2
  N4: Part1.D6_PWM, M1.pin1
  N5: Part1.D7, S1.Pin_3, S1.Pin_4
  N6: Part1.5V, M1.pin3
  N7: R1.Pin_0, LED1.anode
  N8: R2.Pin_0, LED2.anode
